# Fritzing sketch Modulo central (saved by Fritzing 0.9.3b)

parts:
  Part1 = Arduino Nano (Rev3.0)
  JP1 = Header 2 [package=molex-1x2_lock]
  JP2 = Header 2 [package=molex-1x2_lock]
  JP4 = Header 2 [package=molex-1x2_lock]
  JP5 = Header 2 [package=molex-1x2_lock]
  JP6 = Header 2 [package=molex-1x2_lock]
  JP7 = Header 2 [package=molex-1x2_lock]
  JP8 = Header 2 [package=molex-1x2_lock]
  JP9 = Header 2 [package=molex-1x2_lock]
  JP10 = Header 2 [package=molex-1x2_lock]
  JP11 = Header 2 [package=molex-1x2_lock]
  Part2 = NRF24L01
  R2 = Resistor [tolerance=±5% resistance=1k package="2512 [SMD]"]
  R3 = Resistor [tolerance=±5% resistance=1k package="2512 [SMD]"]
  JP12 = Header 3 [package=molex-1x3_lock]
  JP13 = Header 3 [package=molex-1x3_lock]
  JP14 = Header 3 [package=molex-1x3_lock]
  JP15 = Header 3 [package=molex-1x3_lock]
  JP16 = Header 3 [package=molex-1x3_lock]
  JP17 = Header 3 [package=molex-1x3_lock]
  GY1 = GY-5150 (MPU-9150) [form="♀ (female)" package=THT]
  JP18 = Header 2 [package=molex-1x2_lock]
  JP19 = Header 3 [package=molex-1x3_lock]
  U1 = LIPO-2000mAh [package=lipo-2000]
  J2 = BANANA_CONN [package=banana_conn]
  U2 = V_REG_NCP50X [package=dpak-5]
  RE1 = Rotary Encoder [package=THT]
  J3 = Basic Servo
  M2 = ESC
  920KV_Motor2 = DJI 920 KV Motor
  J4 = BANANA_CONN [package=banana_conn]
  S1 = SPST Switch [package=r_sw_th]

nets:
  GND: Part1.GND, JP5.1, JP6.1, JP7.2, JP8.2, JP9.2, JP10.2, JP11.2, Part2.GND, R2.Pin_1, JP14.1, JP15.1, GY1.pin2, JP19.2, U1.-, J2.1, U2.GND, RE1.EncoderPinA, J3.gnd, M2.GND
  N1: Part1.D2, JP15.2, RE1.EncoderPinC
  N2: Part1.D3, JP15.3, RE1.EncoderPinB
  N3: Part1.D5, JP14.2, JP14.3, M2.DATA
  N4: Part1.D6, JP19.3, J3.pulse
  N5: Part1.D9, Part2.MOSI, JP13.1, JP16.1
  N6: Part1.D10, Part2.CSN, JP13.2, JP16.2
  N7: Part1.D11/MOSI, Part2.CE, JP13.3, JP17.1
  N8: Part1.D12/MISO, Part2.SCK, JP12.1, JP17.2
  VIN: Part1.VIN, JP5.2, JP6.2, R3.Pin_1, U2.IN, M2.5V, S1.S
  N9: Part1.A7, R2.Pin_0, R3.Pin_0
  N10: Part1.A5, JP1.2, JP2.2, JP4.2, GY1.pin3, JP18.1
  N11: Part1.A4, JP1.1, JP2.1, JP4.1, GY1.pin4, JP18.2
  3V3: Part1.3V3, Part2.VCC, JP12.3, JP16.3
  N12: Part1.D13/SCK, Part2.MISO, JP12.2, JP17.3
  N13: JP7.1, JP8.1, JP9.1, JP10.1, JP11.1, GY1.pin1, JP19.1, U2.OUT, J3.vcc
  N14: U1.+, S1.P
  N15: M2.U, 920KV_Motor2.u
  N16: M2.V, 920KV_Motor2.v
  N17: M2.W, 920KV_Motor2.w
  N18: J4.1, S1.O

notes:
  Motor brushless MAX10
  Encoder optico
  Ficha banana
  Servo MG996R
  Fuente step down 7.4 - 5V
  NRF24L01
  MPU9250

custom parts:
  GY-5150 (MPU-9150): Placa GY-5150 basada en conjunto de acelerómetro+giroscopios+magnetómetro MPU-9150
  DJI 920 KV Motor: DJI Brushless Outrunner 2212/920K Motor F330-550
