# Fritzing sketch Modulo radar (saved by Fritzing 0.9.3b)

parts:
  Part2 = Arduino Nano (Rev3.0)
  JP21 = Header 2 [package=molex-1x2_lock]
  JP22 = Header 3 [package=molex-1x3_lock]
  JP23 = Header 3 [package=molex-1x3_lock]
  JP24 = Header 3 [package=molex-1x3_lock]
  JP25 = Header 3 [package=molex-1x3_lock]
  JP26 = Header 3 [package=molex-1x3_lock]
  JP27 = Header 2 [package=molex-1x2_lock]
  JP28 = Header 2 [package=molex-1x2_lock]
  JP29 = Header 2 [package=molex-1x2_lock]
  J5 = Infrared Proximity Sensor
  J6 = Basic Servo
  J7 = Infrared Proximity Sensor
  J8 = Infrared Proximity Sensor
  J4 = Infrared Proximity Sensor
  J3 = Infrared Proximity Sensor

nets:
  GND: Part2.GND, JP22.1, JP23.1, JP24.1, JP25.1, JP26.1, JP27.2, JP28.2, J5.GND, J6.gnd, J7.GND, J8.GND, J4.GND, J3.GND
  N1: Part2.D3, JP29.2, J6.pulse
  VCC: Part2.5V, JP22.3, JP23.3, JP24.3, JP25.3, JP26.3, JP27.1, JP28.1, J5.Vcc, J6.vcc, J7.Vcc, J8.Vcc, J4.Vcc, J3.Vcc
  N2: Part2.A7, JP29.1
  N3: Part2.A6, JP26.2, J8.Vout
  N4: Part2.A5, JP21.2
  N5: Part2.A4, JP21.1
  N6: Part2.A3, JP25.2, J7.Vout
  N7: Part2.A2, JP23.2, J5.Vout
  N8: Part2.A1, JP24.2, J4.Vout
  N9: Part2.A0, JP22.2, J3.Vout

notes:
  SENSOR SHARP X5
  SERVO MG966R
