# Fritzing sketch Modulo remoto (saved by Fritzing 0.9.3b)

parts:
  Part1 = Thumb Joystick
  JP27 = Header 3 [package=molex-1x3_lock]
  JP28 = Header 3 [package=molex-1x3_lock]
  Part4 = Arduino Nano (Rev3.0)
  Part5 = NRF24L01

nets:
  GND: Part1.GND, JP28.3, Part4.GND, Part5.GND
  N1: Part1.SEL, JP27.3, Part4.A2
  N2: Part1.HORZ, JP27.1, Part4.A0
  N3: Part1.VERT, JP27.2, Part4.A1
  VCC: Part1.VCC, JP28.1, Part4.5V
  N4: Part4.D9, Part5.MOSI
  N5: Part4.D10, Part5.CSN
  N6: Part4.D11/MOSI, Part5.CE
  N7: Part4.D12/MISO, Part5.SCK
  3V3: Part4.3V3, Part5.VCC
  N8: Part4.D13/SCK, Part5.MISO

notes:
  JOYSTICK
  NRF24L01
